# Fritzing sketch schematic (saved by Fritzing 0.8.7b)
stripboards: 7

parts:
  Bauteil1 = Arduino Mega ADK (Rev3)
  SP1 = SPEAKER [package=pcb_mount_speaker]
  SP2 = SPEAKER [package=pcb_mount_speaker]
  R1 = Photocell (LDR) [package=THT]
  R2 = Resistor [tolerance=±5% resistance=220 package=THT]
  R3 = Photocell (LDR) [package=THT]
  R4 = Resistor [tolerance=±5% resistance=220 package=THT]
  R5 = Photocell (LDR) [package=THT]
  R6 = Resistor [tolerance=±5% resistance=220 package=THT]
  R7 = Photocell (LDR) [package=THT]
  R8 = Resistor [tolerance=±5% resistance=220 package=THT]
  Bauteil2 = Triple Axis Magnetometer - HMC5883 Breakout
  Bauteil3 = Triple Axis Magnetometer - HMC5883 Breakout
  Bauteil4 = Triple Axis Magnetometer - HMC5883 Breakout
  Bauteil5 = Triple Axis Magnetometer - HMC5883 Breakout
  LED1 = LED - 3mm [color="Red (633nm)" package="3 mm [THT]"]
  LED2 = LED - 3mm [color="Green (560nm)" package="3 mm [THT]"]
  LED3 = LED - 3mm [color="Blue (525nm)" package="3 mm [THT]"]
  LED4 = LED - 3mm [color="White (6500K)" package="3 mm [THT]"]
  R9 = Resistor [package="2010 [SMD]"]
  R10 = Resistor [package="2010 [SMD]"]
  R11 = Resistor [package="2010 [SMD]"]
  R12 = Resistor [package="2010 [SMD]"]
  LED5 = LED - 3mm [color="Red (633nm)" package="3 mm [THT]"]
  LED6 = LED - 3mm [color="Green (560nm)" package="3 mm [THT]"]
  LED7 = LED - 3mm [color="Blue (525nm)" package="3 mm [THT]"]
  LED8 = LED - 3mm [color="White (6500K)" package="3 mm [THT]"]
  R13 = Resistor [package="2010 [SMD]"]
  R14 = Resistor [package="2010 [SMD]"]
  R15 = Resistor [package="2010 [SMD]"]
  R16 = Resistor [package="2010 [SMD]"]

nets:
  N1: Bauteil1.A1, R3.pin_1, R4.Pin_0
  N2: Bauteil1.A2, R5.pin_1, R6.Pin_0
  N3: Bauteil1.A3, R7.pin_1, R8.Pin_0
  N4: Bauteil1.D21/SCL, Bauteil2.SCL, Bauteil3.SCL, Bauteil4.SCL, Bauteil5.SCL
  N5: Bauteil1.D20/SDA, Bauteil2.SDA, Bauteil3.SDA, Bauteil4.SDA, Bauteil5.SDA
  N6: Bauteil1.D11_PWM, SP1.-
  N7: Bauteil1.D10_PWM, SP2.-
  N8: Bauteil1.D9_PWM, LED6.cathode, R13.Pin_0, R13.Pin_1
  N9: Bauteil1.D8_PWM, LED6.anode, R16.Pin_0, R16.Pin_1
  VCC: Bauteil1.3V3, Bauteil2.VCC, Bauteil3.VCC, Bauteil4.VCC, Bauteil5.VCC
  N10: Bauteil1.5V, R1.pin_0, R3.pin_0, R5.pin_0, R7.pin_0
  GND: Bauteil1.GND, SP1.+, SP2.+, R2.Pin_1, R4.Pin_1, R6.Pin_1, R8.Pin_1, Bauteil2.GND, Bauteil3.GND, Bauteil4.GND, Bauteil5.GND, LED1.cathode, LED3.cathode, LED3.anode, LED4.cathode, LED4.anode, LED5.cathode, LED7.cathode, LED7.anode, LED8.cathode, LED8.anode
  N11: Bauteil1.D2_PWM, R9.Pin_0, R9.Pin_1
  N12: Bauteil1.D3_PWM, LED1.anode, R10.Pin_0, R10.Pin_1
  N13: Bauteil1.D4_PWM, LED2.anode, R11.Pin_0, R11.Pin_1
  N14: Bauteil1.D5_PWM, LED2.cathode, R12.Pin_0, R12.Pin_1
  N15: Bauteil1.D6_PWM, R15.Pin_0, R15.Pin_1
  N16: Bauteil1.D7_PWM, LED5.anode, R14.Pin_0, R14.Pin_1
  N17: R1.pin_1, R2.Pin_0
